# Fritzing sketch gatecontrol-wifi-unit (saved by Fritzing 0.9.3b)

parts:
  HC-1 = HC-12 Module
  U1 = NodeMCU V3.0

nets:
  N1: HC-1.TXD, U1.D6
  N2: HC-1.RXD, U1.D5
  GND: HC-1.GND, U1.GND
  VCC: HC-1.VCC, U1.3V3

custom parts:
  HC-12 Module: HC-12 433Mhz Module
  NodeMCU V3.0: ESP8266 based NodeMCU
